# Fritzing sketch Sensor de temperatura maqueta (saved by Fritzing 0.9.3b)
breadboards: 2

parts:
  Componente1 = Arduino Uno (Rev3) - ICSP
  T1 = LM35 Temperature Sensor [package="TO92 [THT]"]
  LED1 = LED - 5mm [color="Red (633nm)" package="5 mm [THT]"]
  LED2 = LED - 5mm [color="Red (633nm)" package="5 mm [THT]"]
  LED3 = LED - 5mm [color="Red (633nm)" package="5 mm [THT]"]
  R1 = Resistor [tolerance=±5% resistance=220 package=THT]
  R2 = Resistor [tolerance=±5% resistance=220 package=THT]
  R3 = Resistor [tolerance=±5% resistance=220 package=THT]
  DI1 = 7-Segment LED Display [package=THT]
  R5 = Resistor [tolerance=±5% resistance=220 package=THT]
  R6 = Resistor [tolerance=±5% resistance=220 package=THT]
  R7 = Resistor [tolerance=±5% resistance=220 package=THT]
  R8 = Resistor [tolerance=±5% resistance=220 package=THT]
  R9 = Resistor [tolerance=±5% resistance=220 package=THT]
  R10 = Resistor [tolerance=±5% resistance=220 package=THT]
  R11 = Resistor [tolerance=±5% resistance=220 package=THT]
  R12 = Resistor [tolerance=±5% resistance=220 package=THT]
  R13 = Rotary Potentiometer (Small) [maximum_resistance=100kΩ package=THT]
  DI2 = 7-Segment LED Display [package=THT]
  R14 = Resistor [tolerance=±5% resistance=220 package=THT]
  R15 = Resistor [tolerance=±5% resistance=220 package=THT]
  R16 = Resistor [tolerance=±5% resistance=220 package=THT]
  R17 = Resistor [tolerance=±5% resistance=220 package=THT]
  R18 = Resistor [tolerance=±5% resistance=220 package=THT]
  R19 = Resistor [tolerance=±5% resistance=220 package=THT]

nets:
  N1: Componente1.A0, R13.wiper
  N2: Componente1.A1, R17.Pin_1
  N3: Componente1.A2, R15.Pin_1
  N4: Componente1.A3, T1.Vout
  N5: Componente1.A4/SDA, R19.Pin_1
  N6: Componente1.A5/SCL, R9.Pin_1
  N7: Componente1.ICSP_MISO, Componente1.D12/MISO, R16.Pin_0
  N8: Componente1.D8, R7.Pin_1
  N9: Componente1.D9_PWM, R14.Pin_0
  N10: Componente1.D10_PWM/SS, R1.Pin_0, R2.Pin_0
  N11: Componente1.D11_PWM/MOSI, R3.Pin_0
  N12: Componente1.D13/SCK, R18.Pin_0
  GND: Componente1.GND, T1.GND, LED1.cathode, LED2.cathode, R13.leg2
  N13: Componente1.D2, R5.Pin_1
  N14: Componente1.D3_PWM, R8.Pin_1
  N15: Componente1.D4, R10.Pin_1
  N16: Componente1.D5_PWM, R12.Pin_1
  N17: Componente1.D6_PWM, R6.Pin_1
  N18: Componente1.D7, R11.Pin_1
  N19: Componente1.5V, T1.+Vs, LED3.anode, DI1.commAnode, R13.leg1, DI2.commAnode
  N20: LED1.anode, R2.Pin_1
  N21: LED2.anode, R3.Pin_1
  N22: LED3.cathode, R1.Pin_1
  N23: DI1.cathodeE, R6.Pin_0
  N24: DI1.cathodeD, R11.Pin_0
  N25: DI1.cathodeC, R7.Pin_0
  N26: DI1.cathodeB, R12.Pin_0
  N27: DI1.cathodeA, R10.Pin_0
  N28: DI1.cathodeF, R8.Pin_0
  N29: DI1.cathodeG, R5.Pin_0
  N30: R9.Pin_0, DI2.cathodeG
  N31: DI2.cathodeE, R14.Pin_1
  N32: DI2.cathodeD, R16.Pin_1
  N33: DI2.cathodeC, R18.Pin_1
  N34: DI2.cathodeB, R17.Pin_0
  N35: DI2.cathodeA, R15.Pin_0
  N36: DI2.cathodeF, R19.Pin_0
